# Fritzing sketch blinker (saved by Fritzing 0.9.2b)
breadboards: 1

parts:
  Blinker = Arduino Uno (Rev3)
  LED1 = LED - 5mm [color="Red (633nm)" package="5 mm [THT]"]
  LED2 = LED - 5mm [color="Red (633nm)" package="5 mm [THT]"]
  R1 = Resistor [tolerance=±5% resistance=220 package=THT]
  R2 = Resistor [tolerance=±5% resistance=220 package=THT]

nets:
  N1: Blinker.D12/MISO, R1.Pin_1
  N2: Blinker.D13/SCK, R2.Pin_1
  N3: Blinker.GND, LED1.cathode, LED2.cathode
  N4: LED1.anode, R2.Pin_0
  N5: LED2.anode, R1.Pin_0
